# Fritzing sketch Receiver (saved by Fritzing 0.9.3b)

parts:
  LED = smd LED [color="Red (660nm)" package="0805 [SMD]"]
  Part1 = Arduino Uno (Rev3)
  Lora = Dragino LoRa Shield V1.4

nets:
  GND: LED.cathode, Part1.GND, Lora.GND
  N1: LED.anode, Part1.D13/SCK, Lora.13
  N2: Part1.A0, Lora.A0
  N3: Part1.A1, Lora.A1
  N4: Part1.A2, Lora.A2
  N5: Part1.A3, Lora.A3
  N6: Part1.A4/SDA, Lora.SDA, Lora.A4
  N7: Part1.A5/SCL, Lora.SCL, Lora.A5
  N8: Part1.D8, Lora.8
  N9: Part1.D9_PWM, Lora.9
  N10: Part1.D10_PWM/SS, Lora.10
  N11: Part1.D11_PWM/MOSI, Lora.11
  N12: Part1.D12/MISO, Lora.12
  N13: Part1.AREF, Lora.AREF
  N14: Part1.D0/RX, Lora.0
  N15: Part1.D1/TX, Lora.1
  N16: Part1.D2, Lora.2
  N17: Part1.D3_PWM, Lora.3
  N18: Part1.D4, Lora.4
  N19: Part1.D5_PWM, Lora.5
  N20: Part1.D6_PWM, Lora.6
  N21: Part1.D7, Lora.7
  N22: Part1.ioref, Lora.IOREF
  N23: Part1.RESET, Lora.RST
  3V3: Part1.3V3, Lora.3V3
  5V: Part1.5V, Lora.5V
  VIN: Part1.VIN, Lora.Vin
