# Fritzing sketch Transmitter (saved by Fritzing 0.9.3b)

parts:
  MPU-6050 = GY-521 (MPU-6050) [form="♀ (female)" package=THT]
  Button = Round Pushbutton
  LED2 = LED - 5mm [color="Red (633nm)" package="5 mm [THT]"]
  LED1 = LED - 5mm [color="Green (570nm)" package="5 mm [THT]"]
  Lora = Dragino LoRa Shield V1.4
  Arduino = Arduino Uno (Rev3)

nets (from the schematic view):
  5V: MPU-6050.pin1, Lora.5V, Arduino.5V
  GND: MPU-6050.pin2, Button.leg1, LED2.cathode, LED1.cathode, Lora.GND, Arduino.GND
  N1: MPU-6050.pin3, Lora.A5, Arduino.A5/SCL
  N2: MPU-6050.pin4, Lora.SDA, Lora.A4, Arduino.A4/SDA
  N3: LED2.anode, Arduino.D10_PWM/SS
  N4: LED1.anode, Lora.9, Arduino.D9_PWM
  N5: Lora.AREF, Arduino.AREF
  N6: Lora.13, Arduino.D13/SCK
  N7: Lora.12, Arduino.D12/MISO
  N8: Lora.11, Arduino.D11_PWM/MOSI
  N9: Lora.8, Lora.4, Lora.0, Lora.A0, Lora.ICSP_MISO, Lora.ICSP_GND, Arduino.A0, Arduino.D8, Arduino.D4
  N10: Lora.7, Arduino.D7
  N11: Lora.6, Arduino.D6_PWM
  N12: Lora.5, Arduino.D5_PWM
  N13: Lora.3, Arduino.D3_PWM
  N14: Lora.2, Arduino.D2
  N15: Lora.1, Arduino.D1/TX
  N16: Lora.IOREF, Arduino.ioref
  N17: Lora.RST, Arduino.RESET
  3V3: Lora.3V3, Arduino.3V3
  VIN: Lora.Vin, Arduino.VIN
  N18: Lora.A1, Arduino.A1
  N19: Lora.A2, Arduino.A2
  N20: Lora.A3, Arduino.A3

custom parts:
  GY-521 (MPU-6050): Placa GY-521 basada en conjunto de acelerómetro+giroscopios MPU-6050
